// Logisim project cpu.circ as structural Verilog
module register_bank (
  input  WriteEnable,
  input  [15:0] DstIn,
  input  in_3,
  input  [2:0] DstSel,
  input  [2:0] in_5,
  output [15:0] DstOut,
  output [15:0] SrcOut
);

  wire demultiplexer_1_out0, demultiplexer_1_out1, demultiplexer_1_out2, demultiplexer_1_out3,
       demultiplexer_1_out4, demultiplexer_1_out5, demultiplexer_1_out6, demultiplexer_1_out7, not_1_out;
  wire [15:0] register_1_q, register_2_q, register_3_q, register_4_q, register_5_q, register_6_q,
       register_7_q, register_8_q;

  not not_1 (not_1_out, WriteEnable);
  Demultiplexer #(.select(3)) demultiplexer_1 (
    .out0(demultiplexer_1_out0), .out1(demultiplexer_1_out1), .out2(demultiplexer_1_out2),
    .out3(demultiplexer_1_out3), .out4(demultiplexer_1_out4), .out5(demultiplexer_1_out5),
    .out6(demultiplexer_1_out6), .out7(demultiplexer_1_out7), .in(not_1_out), .sel(DstSel));  // open: en
  Multiplexer #(.select(3), .width(16)) multiplexer_1 (
    .in0(register_1_q), .in1(register_2_q), .in2(register_3_q), .in3(register_4_q), .in4(register_5_q),
    .in5(register_6_q), .in6(register_7_q), .in7(register_8_q), .out(DstOut), .sel(DstSel));  // open: en
  Register #(.width(16)) register_1 (.D(DstIn), .en(demultiplexer_1_out0), .Q(register_1_q), .clk(in_3));  // open: clr
  Multiplexer #(.select(3), .width(16)) multiplexer_2 (
    .in0(register_1_q), .in1(register_2_q), .in2(register_3_q), .in3(register_4_q), .in4(register_5_q),
    .in5(register_6_q), .in6(register_7_q), .in7(register_8_q), .out(SrcOut), .sel(in_5));  // open: en
  Register #(.width(16)) register_2 (.D(DstIn), .en(demultiplexer_1_out1), .Q(register_2_q), .clk(in_3));  // open: clr
  Register #(.width(16)) register_3 (.D(DstIn), .en(demultiplexer_1_out2), .Q(register_3_q), .clk(in_3));  // open: clr
  Register #(.width(16)) register_4 (.D(DstIn), .en(demultiplexer_1_out3), .Q(register_4_q), .clk(in_3));  // open: clr
  Register #(.width(16)) register_5 (.D(DstIn), .en(demultiplexer_1_out4), .Q(register_5_q), .clk(in_3));  // open: clr
  Register #(.width(16)) register_6 (.D(DstIn), .en(demultiplexer_1_out5), .Q(register_6_q), .clk(in_3));  // open: clr
  Register #(.width(16)) register_7 (.D(DstIn), .en(demultiplexer_1_out6), .Q(register_7_q), .clk(in_3));  // open: clr
  Register #(.width(16)) register_8 (.D(DstIn), .en(demultiplexer_1_out7), .Q(register_8_q), .clk(in_3));  // open: clr
endmodule
